// Logisim project NAND.circ as structural Verilog: 1 circuit, main circuit main
module main (
  input  _1,
  input  x,
  input  y,
  input  z
);

  wire nand_1_out, nand_2_out, nand_3_out, nand_4_out, nand_5_out, nand_6_out, nand_7_out, nand_8_out,
       nand_9_out, nand_10_out, nand_11_out, nand_12_out, nand_13_out, nand_14_out, nand_15_out, nand_16_out,
       nand_17_out, nand_18_out, nand_19_out, nand_20_out, nand_21_out, nand_22_out, nand_23_out;

  nand nand_1 (nand_1_out, x, x);
  nand nand_2 (nand_2_out, y, y);
  nand nand_3 (nand_3_out, z, z);
  nand nand_4 (nand_4_out, x, z);
  nand nand_5 (nand_5_out, nand_1_out, nand_3_out);
  nand nand_6 (nand_6_out, nand_2_out, nand_2_out);
  nand nand_7 (nand_7_out, x, y, z);
  nand nand_8 (nand_8_out, nand_1_out, nand_2_out);
  nand nand_9 (nand_9_out, nand_2_out, nand_3_out);
  nand nand_10 (nand_10_out, nand_1_out, nand_3_out);
  nand nand_11 (nand_11_out, x, y);
  nand nand_12 (nand_12_out, nand_1_out, nand_2_out);
  nand nand_13 (nand_13_out, nand_2_out, nand_2_out);
  nand nand_14 (nand_14_out, nand_3_out, nand_3_out);
  nand nand_15 (nand_15_out, x, nand_2_out, z);
  nand nand_16 (nand_16_out, y, nand_3_out);
  nand nand_17 (nand_17_out, nand_7_out, nand_8_out, nand_9_out);
  nand nand_18 (nand_18_out, nand_4_out, nand_5_out, nand_6_out);
  nand nand_19 (nand_19_out, nand_17_out, nand_17_out);
  nand nand_20 (nand_20_out, nand_11_out, nand_12_out);
  nand nand_21 (nand_21_out, nand_13_out, nand_14_out);
  nand nand_22 (nand_22_out, nand_15_out, nand_16_out);
  nand nand_23 (nand_23_out, nand_19_out, nand_10_out);
  _7_Segment_Display u_7_segment_display_1 (
    .g(_1), .f(nand_22_out), .a(nand_18_out), .b(nand_23_out), .e(nand_21_out), .d(nand_23_out),
    .c(nand_20_out));  // open: dp

  // Notes on the sheet:
  //   a
  //   c
  //   e
  //   f
  //   g
  //   d
  //   b
endmodule
