// Logisim project NOR.circ as structural Verilog: 1 circuit, main circuit NOR
module NOR (
  input  _0,
  input  x,
  input  y,
  input  z
);

  wire nor_1_out, nor_2_out, nor_3_out, nor_4_out, nor_5_out, nor_6_out, nor_7_out, nor_8_out, nor_9_out,
       nor_10_out, nor_11_out, nor_12_out, nor_13_out, nor_14_out, nor_15_out, nor_16_out, nor_17_out,
       nor_18_out, nor_19_out, nor_20_out;

  nor nor_1 (nor_1_out, _0, _0);
  nor nor_2 (nor_2_out, x, x);
  nor nor_3 (nor_3_out, y, y);
  nor nor_4 (nor_4_out, z, z);
  nor nor_5 (nor_5_out, x, nor_3_out, nor_4_out);
  nor nor_6 (nor_6_out, nor_2_out, nor_3_out, z);
  nor nor_7 (nor_7_out, x, nor_3_out, nor_4_out);
  nor nor_8 (nor_8_out, nor_2_out, y, nor_4_out);
  nor nor_9 (nor_9_out, nor_2_out, nor_3_out, z);
  nor nor_10 (nor_10_out, x, nor_3_out);
  nor nor_11 (nor_11_out, nor_2_out, y);
  nor nor_12 (nor_12_out, nor_3_out, nor_4_out);
  nor nor_13 (nor_13_out, x, nor_4_out);
  nor nor_14 (nor_14_out, y, z);
  nor nor_15 (nor_15_out, nor_3_out, nor_4_out);
  nor nor_16 (nor_16_out, nor_5_out, nor_6_out);
  nor nor_17 (nor_17_out, nor_7_out, nor_8_out, nor_9_out);
  nor nor_18 (nor_18_out, nor_10_out, nor_11_out);
  nor nor_19 (nor_19_out, nor_12_out, nor_12_out);
  nor nor_20 (nor_20_out, nor_13_out, nor_14_out, nor_15_out);
  _7_Segment_Display u_7_segment_display_1 (
    .g(nor_1_out), .f(nor_20_out), .a(nor_16_out), .b(nor_17_out), .e(nor_19_out), .d(nor_17_out),
    .c(nor_18_out));  // open: dp

  // Notes on the sheet:
  //   a
  //   d
  //   b
  //   c
  //   e
  //   f
  //   g
endmodule
