// Logisim project Sequential circuit.circ as structural Verilog: 1 circuit, main circuit simplified pos sort
module simplified_pos_sort (
  input  w
);

  wire and_1_out, and_2_out, and_3_out, and_4_out, and_5_out, and_6_out, clock_1_out, j_k_ff_1_q, j_k_ff_2_q,
       j_k_ff_3_q, not_1_out, not_2_out, not_3_out, or_1_out, or_2_out, or_3_out, or_4_out, or_5_out,
       or_6_out, or_7_out, or_8_out, undriven;

  and and_1 (and_1_out, j_k_ff_2_q, and_2_out);
  and and_2 (and_2_out, w, j_k_ff_3_q);
  Clock clock_1 (.out(clock_1_out));
  J_K_Flip_Flop j_k_ff_1 (
    .J(and_1_out), .clk(clock_1_out), .K(and_1_out), .Q(j_k_ff_1_q), .preset(undriven), .en(undriven));  // open: Qn, reset
  J_K_Flip_Flop j_k_ff_2 (
    .J(and_2_out), .clk(clock_1_out), .K(and_2_out), .Q(j_k_ff_2_q));  // open: Qn, preset, en, reset
  J_K_Flip_Flop j_k_ff_3 (.J(w), .clk(clock_1_out), .K(w), .Q(j_k_ff_3_q));  // open: Qn, preset, en, reset
  not not_1 (not_1_out, j_k_ff_1_q);
  not not_2 (not_2_out, j_k_ff_2_q);
  not not_3 (not_3_out, j_k_ff_3_q);
  or or_1 (or_1_out, j_k_ff_1_q, not_2_out, not_3_out);
  or or_2 (or_2_out, not_1_out, not_2_out, j_k_ff_3_q);
  or or_3 (or_3_out, not_1_out, j_k_ff_2_q, not_3_out);
  or or_4 (or_4_out, j_k_ff_1_q, not_2_out);
  or or_5 (or_5_out, not_1_out, j_k_ff_2_q);
  or or_6 (or_6_out, not_2_out, not_3_out);
  or or_7 (or_7_out, j_k_ff_1_q, not_3_out);
  or or_8 (or_8_out, j_k_ff_2_q, j_k_ff_3_q);
  and and_3 (and_3_out, or_1_out, or_2_out);
  and and_4 (and_4_out, or_1_out, or_3_out, or_2_out);
  and and_5 (and_5_out, or_4_out, or_5_out);
  and and_6 (and_6_out, or_7_out, or_8_out, or_6_out);
  _7_Segment_Display u_7_segment_display_1 (
    .g(w), .f(and_6_out), .a(and_3_out), .b(and_4_out), .e(or_6_out), .d(and_4_out), .c(and_5_out));  // open: dp

  // Notes on the sheet:
  //   Cw
  //   w
  //   w
  //   B
  //   C
  //   BCw
  //   Cw
  //   A(t+1)
  //   B(t+1)
  //   C(t+1)
  //   x
  //   y
  //   z
  //   x
  //   x'
  //   y'
  //   z'
  //   y'
  //   z
  //   x'
  //   y
  //   z'
  //   x
  //   y'
  //   x'
  //   y
  //   y'
  //   z'
  //   x
  //   z'
  //   y
  //   z
  //   (x+y'+z')
  //   (x'+y'+z)
  //   (x'+y+z')
  //   (x+y')
  //   (x'+y)
  //   (y'+z')
  //   (x+z')
  //   (y+z)
  //   (x+y'+z')
  //   (x'+y'+z)
  //   e
  //   (y'+z')
  //   g
  //   a
  //   b
  //   d
  //   c
  //   f
endmodule
