// Logisim project generalised pos.circ as structural Verilog: 1 circuit, main circuit generalised pos
module generalised_pos (
  input  _0,
  input  x,
  input  y,
  input  z
);

  wire and_1_out, and_2_out, and_3_out, and_4_out, and_5_out, and_6_out, and_7_out, not_1_out, not_2_out,
       not_3_out, not_4_out, or_1_out, or_2_out, or_3_out, or_4_out, or_5_out, or_6_out, or_7_out, or_8_out,
       or_9_out, or_10_out, or_11_out, or_12_out, or_13_out, or_14_out, or_15_out;

  not not_1 (not_1_out, _0);
  not not_2 (not_2_out, x);
  not not_3 (not_3_out, y);
  not not_4 (not_4_out, z);
  or or_1 (or_1_out, x, not_3_out, not_4_out);
  or or_2 (or_2_out, not_2_out, not_3_out, z);
  or or_3 (or_3_out, x, not_3_out, not_4_out);
  or or_4 (or_4_out, not_2_out, y, not_4_out);
  or or_5 (or_5_out, not_2_out, not_3_out, z);
  or or_6 (or_6_out, x, not_3_out, z);
  or or_7 (or_7_out, x, not_3_out, not_4_out);
  or or_8 (or_8_out, not_2_out, y, z);
  or or_9 (or_9_out, not_2_out, y, not_4_out);
  or or_10 (or_10_out, x, not_3_out, not_4_out);
  or or_11 (or_11_out, not_2_out, not_3_out, not_4_out);
  or or_12 (or_12_out, x, y, not_4_out);
  or or_13 (or_13_out, x, not_3_out, not_4_out);
  or or_14 (or_14_out, not_2_out, y, z);
  or or_15 (or_15_out, not_2_out, not_3_out, not_4_out);
  and and_1 (and_1_out, or_1_out, or_2_out);
  and and_2 (and_2_out, or_3_out, or_4_out, or_5_out);
  and and_3 (and_3_out, or_6_out, or_7_out);
  and and_4 (and_4_out, and_3_out, or_8_out, or_9_out);
  and and_5 (and_5_out, or_10_out, or_11_out);
  and and_6 (and_6_out, or_12_out, or_13_out);
  and and_7 (and_7_out, and_6_out, or_14_out, or_15_out);
  _7_Segment_Display u_7_segment_display_1 (
    .g(not_1_out), .f(and_7_out), .a(and_1_out), .b(and_2_out), .e(and_5_out), .d(and_2_out), .c(and_4_out));  // open: dp

  // Notes on the sheet:
  //   a
  //   b
  //   c
  //   e
  //   f
  //   g
  //   d
endmodule
