// Logisim project generalised sop.circ as structural Verilog: 1 circuit, main circuit generalised sop
module generalised_sop (
  input  in_1,
  input  in_2,
  input  in_3
);

  wire and_1_out, and_2_out, and_3_out, and_4_out, and_5_out, and_6_out, and_7_out, and_8_out, and_9_out,
       and_10_out, and_11_out, and_12_out, and_13_out, and_14_out, and_15_out, and_16_out, and_17_out,
       and_18_out, and_19_out, and_20_out, and_21_out, and_22_out, and_23_out, and_24_out, and_25_out,
       and_26_out, and_27_out, not_1_out, not_2_out, not_3_out, or_1_out, or_2_out, or_3_out, or_4_out,
       or_5_out, or_6_out, or_7_out, or_8_out, or_9_out, or_10_out, or_11_out;

  not not_1 (not_1_out, in_1);
  not not_2 (not_2_out, in_2);
  not not_3 (not_3_out, in_3);
  and and_1 (and_1_out, not_1_out, not_2_out, in_3);
  and and_2 (and_2_out, not_1_out, in_2, not_3_out);
  and and_3 (and_3_out, in_1, not_2_out, not_3_out);
  and and_4 (and_4_out, in_1, not_2_out, in_3);
  and and_5 (and_5_out, in_1, in_2, in_3);
  and and_6 (and_6_out, not_1_out, not_2_out, in_3);
  and and_7 (and_7_out, in_1, not_2_out, not_3_out);
  and and_8 (and_8_out, in_1, in_2, in_3);
  and and_9 (and_9_out, not_1_out, in_2, not_3_out);
  and and_10 (and_10_out, not_1_out, not_2_out, in_3);
  and and_11 (and_11_out, in_1, in_2, not_3_out);
  and and_12 (and_12_out, in_1, in_2, in_3);
  and and_13 (and_13_out, not_1_out, not_2_out, in_3);
  and and_14 (and_14_out, not_1_out, in_2, not_3_out);
  and and_15 (and_15_out, in_1, not_2_out, not_3_out);
  and and_16 (and_16_out, in_1, not_2_out, in_3);
  and and_17 (and_17_out, in_1, in_2, not_3_out);
  and and_18 (and_18_out, not_1_out, in_2, not_3_out);
  and and_19 (and_19_out, in_1, not_2_out, in_3);
  and and_20 (and_20_out, in_1, in_2, not_3_out);
  and and_21 (and_21_out, not_1_out, not_2_out, in_3);
  and and_22 (and_22_out, not_1_out, in_2, not_3_out);
  and and_23 (and_23_out, not_1_out, in_2, in_3);
  and and_24 (and_24_out, in_1, not_2_out, not_3_out);
  and and_25 (and_25_out, in_1, not_2_out, in_3);
  and and_26 (and_26_out, in_1, in_2, not_3_out);
  and and_27 (and_27_out, in_1, in_2, in_3);
  or or_1 (or_1_out, and_1_out, and_2_out, and_3_out);
  or or_2 (or_2_out, and_10_out, and_11_out, and_12_out);
  or or_3 (or_3_out, and_13_out, and_14_out, and_15_out);
  or or_4 (or_4_out, or_1_out, and_4_out, and_5_out);
  or or_5 (or_5_out, and_6_out, and_7_out, and_8_out);
  or or_6 (or_6_out, or_3_out, and_16_out, and_17_out);
  or or_7 (or_7_out, and_18_out, and_19_out, and_20_out);
  or or_8 (or_8_out, and_21_out, and_22_out, and_23_out);
  or or_9 (or_9_out, and_25_out, and_26_out, and_27_out);
  or or_10 (or_10_out, or_5_out, and_9_out);
  or or_11 (or_11_out, or_8_out, and_24_out, or_9_out);
  _7_Segment_Display u_7_segment_display_1 (
    .g(or_11_out), .f(or_7_out), .a(or_4_out), .b(or_10_out), .e(or_6_out), .d(or_10_out), .c(or_2_out));  // open: dp

  // Notes on the sheet:
  //   c
  //   e
  //   f
  //   a
  //   d
  //   b
  //   g
endmodule
