// Logisim project multiplexer.circ as structural Verilog: 1 circuit, main circuit multiplexer 
module multiplexer (
  input  in_1,
  input  in_2,
  input  in_3,
  input  in_4,
  input  in_5,
  input  in_6,
  input  in_7,
  input  in_8,
  input  in_9,
  input  in_10,
  input  in_11,
  input  in_12,
  input  in_13,
  input  in_14,
  input  in_15,
  input  in_16,
  input  in_17,
  input  in_18,
  input  in_19,
  input  in_20,
  input  in_21,
  input  in_22,
  input  in_23,
  input  in_24,
  input  in_25,
  input  in_26,
  input  in_27,
  input  in_28,
  input  in_29,
  input  in_30,
  input  in_31,
  input  in_32,
  input  in_33,
  input  in_34,
  input  in_35,
  input  in_36,
  input  in_37,
  input  in_38,
  input  [2:0] in_39,
  input  in_40,
  input  in_41,
  input  in_42,
  input  in_43,
  input  in_44,
  input  in_45,
  input  in_46,
  input  in_47,
  input  in_48,
  input  in_49,
  input  in_50,
  input  in_51
);

  wire multiplexer_1_out, multiplexer_2_out, multiplexer_3_out, multiplexer_4_out, multiplexer_5_out,
       multiplexer_6_out;

  Multiplexer #(.select(3)) multiplexer_1 (
    .in0(in_3), .in1(in_4), .in2(in_5), .in3(in_6), .in4(in_7), .in5(in_8), .in6(in_9), .in7(in_10),
    .out(multiplexer_1_out), .sel(in_39));  // open: en
  Multiplexer #(.select(3)) multiplexer_2 (
    .in0(in_11), .in1(in_12), .in2(in_13), .in3(in_14), .in4(in_15), .in5(in_16), .in6(in_17), .in7(in_18),
    .out(multiplexer_2_out), .sel(in_39));  // open: en
  Multiplexer #(.select(3)) multiplexer_3 (
    .in0(in_19), .in1(in_20), .in2(in_22), .in3(in_24), .in4(in_26), .in5(in_28), .in6(in_30), .in7(in_32),
    .out(multiplexer_3_out), .sel(in_39));  // open: en
  Multiplexer #(.select(3)) multiplexer_4 (
    .in0(in_34), .in1(in_36), .in2(in_37), .in3(in_38), .in4(in_40), .in5(in_41), .in6(in_42), .in7(in_43),
    .out(multiplexer_4_out), .sel(in_39));  // open: en
  Multiplexer #(.select(3)) multiplexer_5 (
    .in0(in_44), .in1(in_45), .in2(in_46), .in3(in_47), .in4(in_48), .in5(in_49), .in6(in_50), .in7(in_51),
    .out(multiplexer_5_out), .sel(in_39));  // open: en
  Multiplexer #(.select(3)) multiplexer_6 (
    .in0(in_21), .in1(in_23), .in2(in_25), .in3(in_27), .in4(in_29), .in5(in_31), .in6(in_33), .in7(in_35),
    .out(multiplexer_6_out), .sel(in_39));  // open: en
  _7_Segment_Display u_7_segment_display_1 (
    .g(multiplexer_6_out), .f(multiplexer_5_out), .a(multiplexer_1_out), .b(multiplexer_2_out),
    .e(multiplexer_4_out), .d(multiplexer_2_out), .c(multiplexer_3_out));  // open: dp

  // Notes on the sheet:
  //   a
  //   d
  //   b
  //   c
  //   e
  //   f
  //   g
  //   g
endmodule
