// Logisim project simplified pos sort.circ as structural Verilog: 1 circuit, main circuit simplified pos sort
module simplified_pos_sort (
  input  x,
  input  y,
  input  z,
  input  x_2
);

  wire and_1_out, and_2_out, and_3_out, and_4_out, not_1_out, not_2_out, not_3_out, not_4_out, or_1_out,
       or_2_out, or_3_out, or_4_out, or_5_out, or_6_out, or_7_out, or_8_out;

  not not_1 (not_1_out, x);
  not not_2 (not_2_out, y);
  not not_3 (not_3_out, z);
  not not_4 (not_4_out, x_2);
  or or_1 (or_1_out, y, not_3_out, not_4_out);
  or or_2 (or_2_out, not_2_out, not_3_out, x_2);
  or or_3 (or_3_out, not_2_out, z, not_4_out);
  or or_4 (or_4_out, y, not_3_out);
  or or_5 (or_5_out, not_2_out, z);
  or or_6 (or_6_out, not_3_out, not_4_out);
  or or_7 (or_7_out, y, not_4_out);
  or or_8 (or_8_out, z, x_2);
  and and_1 (and_1_out, or_1_out, or_2_out);
  and and_2 (and_2_out, or_1_out, or_3_out, or_2_out);
  and and_3 (and_3_out, or_4_out, or_5_out);
  and and_4 (and_4_out, or_7_out, or_8_out, or_6_out);
  _7_Segment_Display u_7_segment_display_1 (
    .g(not_1_out), .f(and_4_out), .a(and_1_out), .b(and_2_out), .e(or_6_out), .d(and_2_out), .c(and_3_out));  // open: dp

  // Notes on the sheet:
  //   0
  //   x'
  //   y'
  //   z'
  //   y'
  //   z
  //   x'
  //   y
  //   z'
  //   x
  //   y'
  //   x'
  //   y
  //   y'
  //   z'
  //   x
  //   z'
  //   y
  //   z
  //   (x+y'+z')
  //   (x'+y'+z)
  //   (x'+y+z')
  //   (x+y')
  //   (x'+y)
  //   (y'+z')
  //   (x+z')
  //   (y+z)
  //   (x+y'+z')
  //   (x'+y'+z)
  //   e
  //   (y'+z')
  //   g
  //   a
  //   d
  //   b
  //   c
  //   f
endmodule
