// Logisim project simplified sop sort.circ as structural Verilog: 1 circuit, main circuit simplified sop sort
module simplified_sop_sort (
  input  x,
  input  y,
  input  z,
  input  x_2
);

  wire and_1_out, and_2_out, and_3_out, and_4_out, and_5_out, and_6_out, and_7_out, and_8_out, not_1_out,
       not_2_out, not_3_out, or_1_out, or_2_out, or_3_out, or_4_out, or_5_out, or_6_out;

  not not_1 (not_1_out, y);
  not not_2 (not_2_out, z);
  not not_3 (not_3_out, x_2);
  and and_1 (and_1_out, y, x_2);
  and and_2 (and_2_out, not_1_out, not_3_out);
  and and_3 (and_3_out, y, z, x_2);
  and and_4 (and_4_out, not_1_out, not_2_out);
  and and_5 (and_5_out, not_2_out, not_3_out);
  and and_6 (and_6_out, y, z);
  or or_1 (or_1_out, not_2_out, not_3_out);
  and and_7 (and_7_out, y, not_2_out, x_2);
  and and_8 (and_8_out, z, not_3_out);
  or or_2 (or_2_out, and_6_out, and_4_out);
  or or_3 (or_3_out, and_3_out, and_4_out);
  or or_4 (or_4_out, and_7_out, and_8_out);
  or or_5 (or_5_out, and_1_out, and_2_out, not_2_out);
  or or_6 (or_6_out, or_3_out, and_5_out, and_2_out);
  _7_Segment_Display u_7_segment_display_1 (
    .g(x), .f(or_4_out), .a(or_5_out), .b(or_6_out), .e(or_1_out), .d(or_6_out), .c(or_2_out));  // open: dp

  // Notes on the sheet:
  //   1
  //   z
  //   x'
  //   z'
  //   x
  //   y
  //   z
  //   x'
  //   y'
  //   y'
  //   z'
  //   x
  //   y
  //   y'
  //   z'
  //   x
  //   y'
  //   z
  //   y
  //   z'
  //   x'z'
  //   y'
  //   xyz
  //   x'y'
  //   y'z'
  //   xy
  //   xy'z
  //   yz'
  //   xz
  //   x'y'
  //   x'z'
  //   c
  //   e
  //   f
  //   g
  //   a
  //   d
  //   b
endmodule
